# Fritzing sketch vmc (saved by Fritzing 0.9.2b)

parts:
  Raspberry_Pi_1 = Raspberry Pi 3
  U1 = 2-Channel 5v Relay Shield [package=relay-2ch5v10a]

nets:
  N1: Raspberry_Pi_1.GIPO23, U1.IN2
  GND: Raspberry_Pi_1.GND, U1.GND, U1.IN1
  5V: Raspberry_Pi_1.5V, U1.VCC
  N2: U1.K1-Off, U1.K2-In

notes:
  Vin
  Speed 2
  Speed 1

custom parts:
  2-Channel 5v Relay Shield: 2 Channel 5v Relay Shield w. 2x SPD-06VDC-SD-C
